# Fritzing sketch sniffer (saved by Fritzing 0.9.2b)
perfboards: 1

parts:
  XTAL1 = Crystal [frequency="16 Mhz" package=THT]
  U1 = ATmega 328P [package=dip]
  J1 = female pin header, 4 pins [form="♀ (female)"]
  R1 = Resistor [tolerance=±5% resistance=68 package=THT]
  C3 = Ceramic Capacitor [package="100 mil [THT, multilayer]"]
  C4 = Ceramic Capacitor [package="100 mil [THT, multilayer]"]
  R4 = Resistor [tolerance=±5% resistance=68 package=THT]
  R5 = Resistor [tolerance=±5% resistance=2.2k package=THT]
  D1 = Rectifier Diode [part_number=1N4001 package="300 mil [THT]"]
  D2 = Rectifier Diode [part_number=1N4001 package="300 mil [THT]"]
  U2 = Voltage Regulator - 5V [package="TO220 [THT]"]
  C5 = Electrolytic Capacitor [capacitance=10µF package="100 mil [THT, electrolytic]"]
  C6 = Electrolytic Capacitor [capacitance=10µF package="100 mil [THT, electrolytic]"]
  R3 = Resistor [tolerance=±5% resistance=10k package=THT]
  J8 = AVR ISP 6 Pin [package=2x3_lock]
  NRF24L1 = NRF24L01

nets (from the schematic view):
  N1: XTAL1.pin_0, U1.PB7_(PCINT7/XTAL2/TOSC2)_[XTAL2], C3.1
  N2: XTAL1.pin_1, U1.PB6_(PCINT6/XTAL1/TOSC1)_[XTAL1], C4.1
  Reset: U1.PC6_(PCINT14/^RESET)_[RESET], R3.Pin_1, J8.5
  N3: U1.PD2_(PCINT18/INT0)_[D2], R1.Pin_1
  N4: U1.PD4_(PCINT20/XCK/T0)_[D4], R4.Pin_1
  5V: U1.VCC, U1.AVCC, J1.pin4, U2.input_voltage, C5.+, R3.Pin_0, J8.2
  GND: U1.GND, J1.pin1, C3.0, C4.0, D2.anode, U2.GND, C5.-, C6.-, J8.6, NRF24L1.GND
  N5: U1.PD5_(PCINT21/OC0B/T1)_[D5_PWM], R5.Pin_1
  N6: U1.PB1_(OC1A/PCINT1)_[D9_PWM], NRF24L1.CE
  N7: U1.PB2_(^SS/OC1B/PCINT2)_[D10_PWM], NRF24L1.CSN
  N8: U1.PB3_(MOSI/OC2A/PCINT3)_[D11_PWM], J8.4, NRF24L1.MOSI
  N9: U1.PB5_(SCK/PCINT5)_[D13], J8.3, NRF24L1.SCK
  N10: U1.AREF, J8.1, NRF24L1.MISO
  N11: J1.pin2, R1.Pin_0, D2.cathode
  N12: J1.pin3, R4.Pin_0, R5.Pin_0, D1.cathode
  N13: U2.output_voltage, C6.+, NRF24L1.VCC

notes:
  Vcc
  GND
  VCC
  GND
  VCC CSN MOSI IRQ
  GND CE SCK MISO
  INPUT OUTPUT GND

custom parts:
  ATmega 328P: Atmel ATmega 328P-PU Microcontroller
  Ceramic Capacitor: 100 nF multilayer Ceramic Capacitor
  NRF24L01: NRF24L01 module
